# Fritzing sketch digital_thermometer (saved by Fritzing 0.7.11b)
breadboards: 1

parts:
  Arduino1 = Arduino
  R1 = Resistor [tolerance=±5% resistance=10k package=THT]
  R2 = Temperature Sensor (Thermistor) [thermistor_type=NTC package=THT]
  DI1 = 7-Segment LED Display [package=THT]
  DI2 = 7-Segment LED Display [package=THT]
  CD4026BE = ULN2003A [package="DIP16 [THT]"]
  CD4026BE_2 = ULN2003A [package="DIP16 [THT]"]

nets:
  N1: Arduino1.GND, R1.Pin_0, DI1.commAnode, DI2.commAnode, CD4026BE.In_2, CD4026BE.0V, CD4026BE_2.In_2, CD4026BE_2.0V
  N2: Arduino1.D3, CD4026BE.Out_2, CD4026BE_2.Out_2
  N3: Arduino1.D2, CD4026BE.In_1
  N4: Arduino1.+5V, R2.pin_1, CD4026BE.In_3, CD4026BE.Out_1, CD4026BE_2.In_3, CD4026BE_2.Out_1
  N5: Arduino1.A0, R1.Pin_1, R2.pin_0
  N6: DI1.cathodeE, CD4026BE_2.Out_6
  N7: DI1.cathodeD, CD4026BE_2.COM_-_Common
  N8: DI1.cathodeC, CD4026BE_2.Out_4
  N9: DI1.cathodeB, CD4026BE_2.Out_5
  N10: DI1.cathodeA, CD4026BE_2.Out_7
  N11: DI1.cathodeF, CD4026BE_2.In_6
  N12: DI1.cathodeG, CD4026BE_2.In_7
  N13: DI2.cathodeE, CD4026BE.Out_6
  N14: DI2.cathodeD, CD4026BE.COM_-_Common
  N15: DI2.cathodeC, CD4026BE.Out_4
  N16: DI2.cathodeB, CD4026BE.Out_5
  N17: DI2.cathodeA, CD4026BE.Out_7
  N18: DI2.cathodeF, CD4026BE.In_6
  N19: DI2.cathodeG, CD4026BE.In_7
  N20: CD4026BE.In_5, CD4026BE_2.In_1
